# Fritzing sketch Schéma électrocardiogramme (saved by Fritzing 0.9.3b)
breadboards: 1

parts:
  Composant1 = Arduino BT
  U1 = LM124-324 Quad Opamp [package="DIP (Dual Inline)"]
  R1 = Resistor [tolerance=±5% resistance=39 package="1206 [SMD]"]
  R2 = Resistor [tolerance=±5% resistance=22k package="1206 [SMD]"]
  R3 = PHOTOCELL [package=photocell]
  R4 = Resistor [tolerance=±5% resistance=68k package="1206 [SMD]"]
  C1 = Capacitor Polarized [package=nippon_f80]
  C2 = Capacitor Polarized [package=cpol-radial-100uf-25v]
  R5 = Resistor [tolerance=±5% resistance=470k package="1206 [SMD]"]
  R6 = Rotary Potentiometer (Small) [maximum_resistance=100kΩ package=THT]
  R7 = Resistor [tolerance=±5% resistance=1k package="1206 [SMD]"]
  LED1 = smd LED [color="Red (633nm)" package="0603 [SMD]"]
  LED2 = smd LED [color="Red (633nm)" package="0603 [SMD]"]
  R8 = Resistor [tolerance=±5% resistance=100 package="1206 [SMD]"]

nets:
  N1: Composant1.GND, U1.VCC-, R3.P$1, R4.Pin_0, C2.-, R5.Pin_0, R6.leg1, R7.Pin_0, LED1.cathode, LED2.cathode, R8.Pin_0
  N2: Composant1.A0, LED2.anode, R8.Pin_1
  N3: Composant1.A1, R6.wiper
  N4: Composant1.5V, U1.VCC+, R1.Pin_1, R2.Pin_1, R6.leg2
  N5: U1.2IN+, R4.Pin_1, C1.-
  N6: U1.2IN-, C2.+, R5.Pin_1, R7.Pin_1
  N7: R1.Pin_0, LED1.anode
  N8: R2.Pin_0, R3.P$2, C1.+
